# Fritzing sketch FlapBoxFritzingSketch (saved by Fritzing 0.9.2b)
breadboards: 1

parts:
  Composant2 = Arduino Nano (Rev3.0)
  NRF24L2 = NRF24L01
  Raspberry_Pi_1 = Raspberry Pi 3 [part_number=RPI-3-V1.2]  # not connected

nets:
  GND: Composant2.GND, NRF24L2.GND
  N1: Composant2.D7, NRF24L2.CSN
  N2: Composant2.D8, NRF24L2.CE
  N3: Composant2.D11/MOSI, NRF24L2.MOSI
  N4: Composant2.D12/MISO, NRF24L2.MISO
  3V3: Composant2.3V3, NRF24L2.VCC
  N5: Composant2.D13/SCK, NRF24L2.SCK

custom parts:
  NRF24L01: NRF24L01 module
